# Fritzing sketch diagrama en fritzing (saved by Fritzing 0.8.7b)

parts:
  M1 = DC Motor
  VCC1 = Battery block 9V
  S1 = H-Bridge with L298N
  M2 = DC Motor
  Part1 = Arduino Uno (Rev3)
  Raspberry_Pi_1 = Raspberry Pi 3  # not connected
  VCC2 = 4 x AAA Battery Mount  # not connected

nets:
  N1: M1.pin_1, S1.M2-02
  N2: M1.pin_2, S1.M2-01
  N3: VCC1.-, Part1.GND
  N4: VCC1.+, S1.12V
  N5: S1.IN1, Part1.D7
  N6: S1.IN2, Part1.D6_PWM
  N7: S1.IN3, Part1.D5_PWM
  N8: S1.IN4, Part1.D4
  N9: S1.M1-01, M2.pin_2
  N10: S1.M1-02, M2.pin_1

custom parts:
  H-Bridge with L298N: h-bridge
